// Digital circuit BW8comp.dig as structural Verilog
module BW8comp (
  input  Crystal,
  input  _555,
  input  Step
);

  wire addr_bus, clk_cpu, clk_crystal, dbg, mem_bus, nbreak, nbrk, ndemo, nrst, nrun, triple_clock_1_clk_cpu;

  Button #(.activeLow("true")) Run (.out(nrun));
  Button #(.activeLow("true")) Demo (.out(ndemo));
  Button #(.activeLow("true")) Break (.out(nbreak));
  triple_clock triple_clock_1 (
    .nrun(nrun), .ndemo(ndemo), .nbreak(nbreak), .crystal(Crystal), ._555(_555), .step(Step), .nbrk(nbrk),
    .nrun_rst(nrst), .ndemo_rst(1'b1), .nstep_rst(1'b1), .clk_cpu(triple_clock_1_clk_cpu),
    .clk_crystal(clk_crystal));
  Reset reset_1 (.out(nrst));
  LED led_1 (.in(clk_cpu));
  LED led_2 (.in(clk_crystal));
  // BW8cpu bw8cpu_1: pin names not known; wires that end beside it: 1'b1, 1'b0, triple_clock_1_clk_cpu, nrst, 1'b1, 1'b1, addr_bus, mem_bus, 1'b1, 1'b1, nbrk, dbg

  // Other names for the same wires on the sheet: clk_step = Step; rst_clk_mode[2] = nrst

  // Notes on the sheet:
  //   Crystal: Hz: 5
endmodule
