// Digital circuit BW8cpu.dig as structural Verilog
module BW8cpu (
  input  VCC,
  input  GND,
  input  step,
  input  crystal,
  input  _555,
  output [15:0] ADDR,
  output nBRK,
  output [7:0] Mem_Bus
);

  wire a_dbus_a, a_dbus_l, a_lhs_a, a_rhs_a, ab_xfer_l, ack_addr_a, addr_inc, addr_xfer_a, alu_dbus_a,
       b_dbus_a, b_dbus_l, b_lhs_a, b_rhs_a, c_dbus_a, c_dbus_l, c_lhs_a, c_rhs_a, cd_xfer_l, clk,
       clk_crystal, d_dbus_a, d_dbus_l, d_lhs_a, d_rhs_a, da_dbus_a, da_dbus_l, dec_sp, dp_addr_a, dp_dbus_a,
       dp_dbus_l, ext, io_addr_a, ir_dbus_l, isr_xfer_a, lsb_dbus_a, mem_dbus_a, mem_dbus_l, msb_dbus_a,
       nclk, noffset, nrst, nRST_out, off_dbus_l, pc_addr_a, pc_inc, pc_xfer_a, pc_xfer_l, pch_dbus_l,
       pcl_dbus_l, reg_pc, reg_sp, reg_x, reg_y, rst, sp_addr_a, sp_dec, sp_inc, sp_xfer_a, sp_xfer_l,
       sph_dbus_l, spl_dbus_l, sr_dbus_a, sr_dbus_l, t_addr_a, th_dbus_a, th_dbus_l, th_lhs_a, tl_dbus_a,
       tl_dbus_l, tl_rhs_a, x_addr_a, x_dec, x_inc, x_xfer_a, x_xfer_l, xh_dbus_l, xl_dbus_l, y_addr_a,
       y_dec, y_inc, y_xfer_a, y_xfer_l, yh_dbus_l, yl_dbus_l;
  wire [2:0] addr_a, Break_out, clk_mode, count, t_state, xfer_l;
  wire [3:0] alu_op, dbus_a;
  wire [4:0] dbus_l, flags, xfer_a;
  wire [7:0] alu_res, dbus, lhs, opcode, reg_a, reg_b, reg_c, reg_d, reg_da, reg_dp, reg_off, reg_th, reg_tl,
       rhs;
  wire [15:0] addr_t;
  wire [17:3] Control_Unit_dbg;

  // Probe on dbus
  // Probe on {lhs, rhs}
  // Probe on reg_a
  // Probe on reg_b
  // Probe on reg_c
  // Probe on reg_d
  // Probe on reg_dp
  // Probe on reg_da
  // Probe on reg_tl
  // Probe on reg_th
  // Probe C_f on flags[4]
  // Probe Z_f on flags[3]
  PowerSupply powersupply_1 (.VDD(VCC), .GND(GND));
  // Probe on addr_t
  // Probe on Mem_Bus
  // Probe on reg_pc
  // Probe on reg_sp
  // Probe on reg_x
  // Probe on reg_y
  // Probe on reg_off
  // Probe on alu_res
  // Probe N_f on flags[1]
  // Probe V_f on flags[2]
  // Probe I_f on flags[0]
  // Probe on opcode
  // Probe on ext
  Button u_nRST (.out(nRST_out));
  Button #(.activeLow("true")) Run (.out(Break_out[0]));
  Button #(.activeLow("true")) Demo (.out(Break_out[1]));
  Button #(.activeLow("true")) Break (.out(Break_out[2]));
  // Probe on flags
  control_unit Control_Unit (
    .nirq(1'b1), .opcode(opcode), .flags(flags), .nreq(1'b1), .clk(clk), .nrst(nrst), .nnmi(1'b1),
    .dbus_assert(dbus_a), .dbus_load(dbus_l), .alu_op(alu_op), .xfer_assert(xfer_a), .xfer_load(xfer_l),
    .addr_assert(addr_a), .count(count), .dec_sp(dec_sp), .nbrk(nBRK), .nclk(nclk), .noffset(noffset),
    .rst(rst), .dbg({Control_Unit_dbg[17:16], ext, Control_Unit_dbg[14:3], t_state}));
  instruction_register Instruction_Register (
    .dbus(dbus), .ndbus_load(ir_dbus_l), .clr(rst), .nclk(nclk), .opcode(opcode));
  memory_bridge Memory_Bridge (.dbus_assert(mem_dbus_a), .dbus_load(mem_dbus_l), .dbus(dbus), .mbus(Mem_Bus));
  ROM #(.AddrBits(16), .isProgramMemory("true"), .Bits(8)) ROM (.A(ADDR), .sel(1'b1), .D(Mem_Bus));
  reset_module reset_module_1 (.clk(clk_crystal), .nrst_in(nRST_out), .nrst(nrst));
  // Probe on t_state
  // triple_clock triple_clock_1: pin names not known; wires that end beside it: Break_out, nBRK, {nrst, 2'b11}, crystal, _555, step, clk, clk_crystal, clk_mode
  // Probe on nclk
  // Probe on nBRK
  LED Run_Mode_Active (.in(clk_mode[0]));
  LED Demo_Mode_Active (.in(clk_mode[1]));
  LED Break_Mode_Active (.in(clk_mode[2]));
  // Probe on dec_sp
  LED cpu (.in(clk));
  LED u_crystal (.in(clk_crystal));
  // Probe on count
  // Probe on addr_a
  // Probe on xfer_l
  bus_controller Bus_Controller (
    .dbus_assert(dbus_a), .xfer_load(xfer_l), .addr_assert(addr_a), .clk(clk), .count(count),
    .dec_sp(dec_sp), .nclk(nclk), .dbus_load(dbus_l), .xfer_assert(xfer_a), .ALU_dbus_assert(alu_dbus_a),
    .A_dbus_assert(a_dbus_a), .B_dbus_assert(b_dbus_a), .C_dbus_assert(c_dbus_a), .D_dbus_assert(d_dbus_a),
    .DP_dbus_assert(dp_dbus_a), .DA_dbus_assert(da_dbus_a), .TH_dbus_assert(th_dbus_a),
    .TL_dbus_assert(tl_dbus_a), .SR_dbus_assert(sr_dbus_a), .MEM_dbus_assert(mem_dbus_a),
    .MSB_dbus_assert(msb_dbus_a), .LSB_dbus_assert(lsb_dbus_a), .A_dbus_load(a_dbus_l),
    .B_dbus_load(b_dbus_l), .C_dbus_load(c_dbus_l), .D_dbus_load(d_dbus_l), .DP_dbus_load(dp_dbus_l),
    .DA_dbus_load(da_dbus_l), .TH_dbus_load(th_dbus_l), .TL_dbus_load(tl_dbus_l), .SR_dbus_load(sr_dbus_l),
    .MEM_dbus_load(mem_dbus_l), .IR_dbus_load(ir_dbus_l), .OFF_dbus_load(off_dbus_l),
    .PCH_dbus_load(pch_dbus_l), .PCL_dbus_load(pcl_dbus_l), .SPH_dbus_load(sph_dbus_l),
    .SPL_dbus_load(spl_dbus_l), .XH_dbus_load(xh_dbus_l), .XL_dbus_load(xl_dbus_l), .YH_dbus_load(yh_dbus_l),
    .YL_dbus_load(yl_dbus_l), .PC_xfer_assert(pc_xfer_a), .SP_xfer_assert(sp_xfer_a),
    .X_xfer_assert(x_xfer_a), .Y_xfer_assert(y_xfer_a), .ISR_xfer_assert(isr_xfer_a),
    .addr_xfer_assert(addr_xfer_a), .A_lhs_assert(a_lhs_a), .B_lhs_assert(b_lhs_a), .C_lhs_assert(c_lhs_a),
    .D_lhs_assert(d_lhs_a), .TH_lhs_assert(th_lhs_a), .A_rhs_assert(a_rhs_a), .B_rhs_assert(b_rhs_a),
    .C_rhs_assert(c_rhs_a), .D_rhs_assert(d_rhs_a), .TL_rhs_assert(tl_rhs_a), .PC_xfer_load(pc_xfer_l),
    .SP_xfer_load(sp_xfer_l), .X_xfer_load(x_xfer_l), .Y_xfer_load(y_xfer_l), .AB_xfer_load(ab_xfer_l),
    .CD_xfer_load(cd_xfer_l), .ACK_addr_assert(ack_addr_a), .PC_addr_assert(pc_addr_a),
    .SP_addr_assert(sp_addr_a), .X_addr_assert(x_addr_a), .Y_addr_assert(y_addr_a),
    .DP_addr_assert(dp_addr_a), .T_addr_assert(t_addr_a), .IO_addr_assert(io_addr_a), .PC_inc(pc_inc),
    .SP_inc(sp_inc), .X_inc(x_inc), .Y_inc(y_inc), .ADDR_inc(addr_inc), .X_dec(x_dec), .Y_dec(y_dec),
    .SP_dec(sp_dec));
  // Probe on xfer_a
  // Probe on alu_op
  // Probe on dbus_l
  // Probe on dbus_a
  alu Arithmetic___Logic_Unit_and_Status_Register (
    .alu_op(alu_op), .load_sr_dbus(sr_dbus_l), .assert_sr_dbus(sr_dbus_a), .clk(nclk), .clr(rst), .lhs(lhs),
    .rhs(rhs), .assert_alu_dbus(alu_dbus_a), .flags(flags), .dbus(dbus), .q(alu_res));
  gpr_pair A_and_B (
    .naddr_assert(1'b1), .nxfer_load(ab_xfer_l), .nhi_dbus_load(a_dbus_l), .nlo_dbus_load(b_dbus_l),
    .nhi_dbus_assert(a_dbus_a), .nlo_dbus_assert(b_dbus_a), .nhi_lhs_assert(a_lhs_a),
    .nlo_lhs_assert(b_lhs_a), .nhi_rhs_assert(a_rhs_a), .nlo_rhs_assert(b_rhs_a), .dbus(dbus),
    .xfer({lhs, rhs}), .clr(rst), .nclk(nclk), .reg_hi(reg_a), .reg_lo(reg_b));  // open: addr
  gpr_pair C_and_D (
    .naddr_assert(1'b1), .nxfer_load(cd_xfer_l), .nhi_dbus_load(c_dbus_l), .nlo_dbus_load(d_dbus_l),
    .nhi_dbus_assert(c_dbus_a), .nlo_dbus_assert(d_dbus_a), .nhi_lhs_assert(c_lhs_a),
    .nlo_lhs_assert(d_lhs_a), .nhi_rhs_assert(c_rhs_a), .nlo_rhs_assert(d_rhs_a), .dbus(dbus),
    .xfer({lhs, rhs}), .clr(rst), .nclk(nclk), .reg_hi(reg_c), .reg_lo(reg_d));  // open: addr
  gpr_pair DA_and_DP (
    .naddr_assert(1'b1), .nxfer_load(1'b1), .nhi_dbus_load(dp_dbus_l), .nlo_dbus_load(da_dbus_l),
    .nhi_dbus_assert(dp_dbus_a), .nlo_dbus_assert(da_dbus_a), .nhi_lhs_assert(1'b1), .nlo_lhs_assert(1'b1),
    .nhi_rhs_assert(1'b1), .nlo_rhs_assert(1'b1), .dbus(dbus), .xfer({lhs, rhs}), .clr(rst), .nclk(nclk),
    .reg_hi(reg_dp), .reg_lo(reg_da));  // open: addr
  gpr_pair TH_and_TL (
    .naddr_assert(t_addr_a), .nxfer_load(1'b1), .nhi_dbus_load(th_dbus_l), .nlo_dbus_load(tl_dbus_l),
    .nhi_dbus_assert(th_dbus_a), .nlo_dbus_assert(tl_dbus_a), .nhi_lhs_assert(th_lhs_a),
    .nlo_lhs_assert(1'b1), .nhi_rhs_assert(1'b1), .nlo_rhs_assert(tl_rhs_a), .dbus(dbus), .xfer({lhs, rhs}),
    .clr(rst), .nclk(nclk), .reg_hi(reg_th), .reg_lo(reg_tl));  // open: addr
  // address_register Program_Counter: pin names not known; wires that end beside it: clk, rst, pc_inc, 1'b1, pc_xfer_l, pc_addr_a, pc_xfer_a, pch_dbus_l, pcl_dbus_l, dbus, addr_t, {lhs, rhs}, reg_pc
  // address_register Stack_Pointer: pin names not known; wires that end beside it: clk, rst, sp_inc, 1'b1, sp_xfer_l, sp_addr_a, sp_xfer_a, sph_dbus_l, spl_dbus_l, dbus, addr_t, {lhs, rhs}, reg_sp
  // address_register X_Index: pin names not known; wires that end beside it: clk, rst, x_inc, 1'b1, x_xfer_l, x_addr_a, x_xfer_a, xh_dbus_l, xl_dbus_l, dbus, addr_t, {lhs, rhs}, reg_x
  // address_register Y_Index: pin names not known; wires that end beside it: clk, rst, y_inc, 1'b1, y_xfer_l, y_addr_a, y_xfer_a, yh_dbus_l, yl_dbus_l, dbus, addr_t, {lhs, rhs}, reg_y
  address_offset Address_Bridge (
    .nclk(off_dbus_l), .dbus(dbus), .addr_in(addr_t), .noffset_en(1'b1), .carry_en(1'b0),
    .naddr_xfer_assert(1'b1), .nassert_addr(ack_addr_a), .nclr(nrst), .addr_out(ADDR), .xfer({lhs, rhs}),
    .q(reg_off));

  // Other names for the same wires on the sheet: addr_out[15:0] = ADDR; clk_cpu = clk; mbus[7:0] = Mem_Bus;
  //   rst_clk_mode[2] = nrst; xfer[15:0] = {lhs, rhs}

  // Notes on the sheet:
  //   VCC: default 1
  //   crystal: Hz: 5
  //   External Pinout
  //   Buses & Constants
  //   Registers
  //   ROM loads test.bin
endmodule
