// Digital circuit alu.dig as structural Verilog
module alu (
  input  [4:0] alu_op
);

  alu_shift_unit alu_shift_unit_1 ();  // open: shift_func_sel, lhs, C_fin, Q, C_fout
  alu_arithmetic_unit alu_arithmetic_unit_1 ();  // open: left, right, C_fin
  alu_logic_unit alu_logic_unit_1 ();  // open: logic_func_sel, rhs, lhs, Q
endmodule
