// Digital circuit alu_arithmetic_unit.dig as structural Verilog
module alu_arithmetic_unit (
  input  [7:0] left,
  input  [7:0] right,
  input  C_fin
);

  wire _74ls283_1_c_out, C_fout;
  wire [3:0] s_hi, s_lo;

  _74ls283 _74ls283_1 (
    .A(left[3:0]), .B(right[3:0]), .C_in(C_fin), .VCC(1'b1), .GND(1'b0), .S(s_lo), .C_out(_74ls283_1_c_out));
  _74ls283 _74ls283_2 (
    .A(left[7:4]), .B(right[7:4]), .C_in(_74ls283_1_c_out), .VCC(1'b1), .GND(1'b0), .S(s_hi), .C_out(C_fout));

  // Other names for the same wires on the sheet: left_lo[3:0] = left[3:0]; left_hi[3:0] = left[7:4];
  //   right_lo[3:0] = right[3:0]; right_hi[3:0] = right[7:4]
endmodule
