// Digital circuit direct_page_register.dig as structural Verilog
module direct_page_register (
  input  [7:0] dbus,
  input  clk,
  input  clr,
  input  [7:0] rhs,
  input  [15:0] addr,
  input  assert_addr,
  input  assert_t1_dbus,
  input  assert_t1_rhs,
  input  assert_dp_dbus,
  input  load_t1_dbus,
  input  load_dp_dbus,
  output [7:0] reg_dp,
  output [7:0] reg_t1
);

  wire [7:0] addr_hi, addr_lo;

  // _74ls173 T1_hi: pin names not known; wires that end beside it: dbus[7:4], 1'b1, 1'b0, clr, clk, load_t1_dbus, load_t1_dbus, 1'b0, 1'b0, reg_t1[7:4]
  // _74ls173 DP_hi: pin names not known; wires that end beside it: dbus[7:4], 1'b1, 1'b0, clr, clk, load_dp_dbus, load_dp_dbus, 1'b0, 1'b0, reg_dp[7:4]
  // _74ls173 T1_lo: pin names not known; wires that end beside it: dbus[3:0], 1'b1, 1'b0, clr, clk, load_t1_dbus, load_t1_dbus, 1'b0, 1'b0, reg_t1[3:0]
  // _74ls173 DP_lo: pin names not known; wires that end beside it: dbus[3:0], 1'b1, 1'b0, clr, clk, load_dp_dbus, load_dp_dbus, 1'b0, 1'b0, reg_dp[3:0]
  _74ls245 T1_to_dbus (.DIR(1'b1), .nOE(assert_t1_dbus), .A(reg_t1), .B(dbus), .VCC(1'b1), .GND(1'b0));
  _74ls245 DP_to_dbus (.DIR(1'b1), .nOE(assert_dp_dbus), .A(reg_dp), .B(dbus), .VCC(1'b1), .GND(1'b0));
  _74ls245 T1_to_addr (.DIR(1'b1), .nOE(assert_addr), .A(reg_t1), .B(addr_lo), .VCC(1'b1), .GND(1'b0));
  _74ls245 DP_to_addr (.DIR(1'b1), .nOE(assert_addr), .A(reg_dp), .B(addr_hi), .VCC(1'b1), .GND(1'b0));
  _74ls245 T1_to_rhs (.DIR(1'b1), .nOE(assert_t1_rhs), .A(reg_t1), .B(rhs), .VCC(1'b1), .GND(1'b0));

  // Other names for the same wires on the sheet: d_lo[3:0] = dbus[3:0]; d_hi[3:0] = dbus[7:4];
  //   q_00[3:0] = reg_t1[3:0]; q_t1[7:0] = reg_t1; q_01[3:0] = reg_t1[7:4]; q_10[3:0] = reg_dp[3:0];
  //   q_dp[7:0] = reg_dp; q_11[3:0] = reg_dp[7:4]
endmodule
