// Digital circuit general_purpose_register.dig as structural Verilog
module general_purpose_register (
  input  dbus_load,
  input  dbus_assert,
  input  lhs_assert,
  input  rhs_assert,
  input  nclr,
  input  [7:0] dbus,
  output [7:0] lhs,
  output [7:0] rhs,
  output [7:0] \reg 
);

  _74ls273 _74ls273_1 (.CP(dbus_load), .nMR(nclr), .D(dbus), .VCC(1'b1), .GND(1'b0), .Q(\reg ));
  _74ls245 to_dbus (.DIR(1'b1), .nOE(dbus_assert), .A(\reg ), .B(dbus), .VCC(1'b1), .GND(1'b0));
  _74ls245 to_lhs (.DIR(1'b1), .nOE(lhs_assert), .A(\reg ), .B(lhs), .VCC(1'b1), .GND(1'b0));
  _74ls245 to_rhs (.DIR(1'b1), .nOE(rhs_assert), .A(\reg ), .B(rhs), .VCC(1'b1), .GND(1'b0));

  // Other names for the same wires on the sheet: q[7:0] = \reg 

  // Notes on the sheet:
  //   dbus_load: default 1
  //   dbus_assert: default 1
  //   lhs_assert: default 1
  //   rhs_assert: default 1
endmodule
