// Digital circuit instruction_register.dig as structural Verilog
module instruction_register (
  input  [7:0] dbus,
  input  ndbus_load,
  input  clr,
  input  nclk,
  output [7:0] opcode
);

  // _74ls173 _74ls173_1: pin names not known; wires that end beside it: dbus[7:4], clr, nclk, ndbus_load, ndbus_load, 1'b0, 1'b0, 1'b1, 1'b0, opcode[7:4]
  // _74ls173 _74ls173_2: pin names not known; wires that end beside it: dbus[3:0], clr, nclk, ndbus_load, ndbus_load, 1'b0, 1'b0, 1'b1, 1'b0, opcode[3:0]

  // Other names for the same wires on the sheet: lo[3:0] = dbus[3:0]; hi[3:0] = dbus[7:4]; nload = ndbus_load
endmodule
